// Logisim project projeto_mips_pipeline.circ as structural Verilog: 13 circuits, main circuit main
module main (
);

  wire and_2_out, clock_1_out, not_1_out, or_2_out, reg_ex_mem_1_memory_write_2, reg_ex_mem_1_memtoreg_2,
       reg_ex_mem_1_regwrite_2, reg_id_ex_1_alusrc_2, reg_id_ex_1_branch_2, reg_id_ex_1_branch_select_2,
       reg_id_ex_1_jump_2, reg_id_ex_1_memread_2, reg_id_ex_1_memtoreg_2, reg_id_ex_1_memwrite_2,
       reg_id_ex_1_regdest_2, reg_id_ex_1_regwrite_2, reg_mem_wb_1_memtoreg_2, reg_mem_wb_1_reg_write_2,
       uc_w_1_alusrc, uc_w_1_branch, uc_w_1_branch_select, uc_w_1_jr, uc_w_1_jump, uc_w_1_link,
       uc_w_1_memread, uc_w_1_memtoreg, uc_w_1_memwrite, uc_w_1_regdest, uc_w_1_regwrite, ula_1_igual,
       unid_hazard_1_stall, xor_1_out;
  wire [1:0] and_1_out, fowarding_1_forward_a, fowarding_1_forward_b;
  wire [2:0] reg_id_ex_1_aluop_2, uc_w_1_aluop;
  wire [4:0] multiplexer_3_out, reg_ex_mem_1_write_register_2, reg_id_ex_1_rd_2, reg_id_ex_1_rs_2,
       reg_id_ex_1_rt_2, reg_mem_wb_1_write_register_2;
  wire [5:0] alu_control_1_out_3;
  wire [31:0] adder_1_out, adder_2_out, adder_3_out, banco_registradores_1_r1, banco_registradores_1_r2,
       bit_extender_1_out, DATA_MEMORY_data, INSTRUCTION_MEMORY_data, multiplexer_1_out, multiplexer_2_out,
       multiplexer_4_out, multiplexer_5_out, multiplexer_6_out, multiplexer_7_out, PC_q,
       reg_ex_mem_1_alu_out_2, reg_ex_mem_1_branch_address_2, reg_ex_mem_1_data_rt_2, reg_id_ex_1_data_rs_2,
       reg_id_ex_1_data_rt_2, reg_id_ex_1_imext_2, reg_id_ex_1_pc_4_2, reg_if_id_1_out_5, reg_if_id_1_out_6,
       reg_mem_wb_1_alu_out_2, reg_mem_wb_1_mem_out_2, shifter_1_out, ula_1_resultado;

  or or_1 (and_1_out[1], reg_id_ex_1_jump_2, uc_w_1_jr);
  not not_1 (not_1_out, uc_w_1_jr);
  or or_2 (or_2_out, reg_id_ex_1_jump_2, and_2_out);
  Multiplexer #(.width(32), .enable("false")) multiplexer_1 (
    .in0(multiplexer_2_out), .in1(PC_q), .out(multiplexer_1_out), .sel(unid_hazard_1_stall));
  Multiplexer #(.select(2), .width(32), .enable("false")) multiplexer_2 (
    .in0(adder_1_out), .in1(reg_ex_mem_1_branch_address_2),
    .in2({PC_q[31:28], reg_if_id_1_out_6[25:21], reg_if_id_1_out_6[25:21], reg_if_id_1_out_6[15:0], 2'b00}),
    .in3(multiplexer_4_out), .out(multiplexer_2_out), .sel(and_1_out));
  and and_1 (and_1_out[0], not_1_out, or_2_out);
  Register #(.width(32), .Select("low")) PC (
    .D(multiplexer_1_out), .Q(PC_q), .clk(clock_1_out), .clr(unid_hazard_1_stall));  // open: en
  Adder #(.width(32)) adder_1 (.a(32'h4), .b(PC_q), .out(adder_1_out));  // open: cin, cout
  RAM #(.addrWidth(16), .dataWidth(32), .Select("high"), .simpleMode("false")) INSTRUCTION_MEMORY (
    .addr(PC_q[17:2]), .data(INSTRUCTION_MEMORY_data), .clk(clock_1_out));  // open: sel, ld, clr
  REG_IF_ID reg_if_id_1 (
    .in_1(adder_1_out), .in_2(INSTRUCTION_MEMORY_data), .out_5(reg_if_id_1_out_5),
    .out_6({reg_if_id_1_out_6[31:21], reg_if_id_1_out_6[25:21], reg_if_id_1_out_6[15:0]}), .CLK(clock_1_out),
    .STALL(unid_hazard_1_stall));
  UNID_HAZARD unid_hazard_1 (
    .STALL(unid_hazard_1_stall), .REG_RT_ID_EX(reg_id_ex_1_rt_2), .REG_RT_IF_ID(reg_if_id_1_out_6[25:21]),
    .REG_RS_IF_ID(reg_if_id_1_out_6[25:21]), .MEMREAD(reg_id_ex_1_memread_2));
  UC_W uc_w_1 (
    .in_1(reg_if_id_1_out_6[31:26]), .REGDEST(uc_w_1_regdest), .JUMP(uc_w_1_jump), .BRANCH(uc_w_1_branch),
    .MEMTOREG(uc_w_1_memtoreg), .ALUOP(uc_w_1_aluop), .MEMWRITE(uc_w_1_memwrite), .ALUSRC(uc_w_1_alusrc),
    .REGWRITE(uc_w_1_regwrite), .BRANCH_SELECT(uc_w_1_branch_select), .JR(uc_w_1_jr), .LINK(uc_w_1_link),
    .MEMREAD(uc_w_1_memread));
  banco_registradores banco_registradores_1 (
    .R1_num(reg_if_id_1_out_6[25:21]), .R2_num(reg_if_id_1_out_6[25:21]), .RW(reg_mem_wb_1_write_register_2),
    .Din(multiplexer_7_out), .WE(reg_mem_wb_1_reg_write_2), .clk(clock_1_out), .R1(banco_registradores_1_r1),
    .R2(banco_registradores_1_r2), .JAL(adder_2_out), .LINK(uc_w_1_link));
  assign bit_extender_1_out = {{16{reg_if_id_1_out_6[15]}}, reg_if_id_1_out_6[15:0]};  // Bit_Extender bit_extender_1
  Clock clock_1 (.out(clock_1_out));
  Adder #(.width(32)) adder_2 (.a(PC_q), .b(32'h1), .out(adder_2_out));  // open: cin, cout
  REG_ID_EX reg_id_ex_1 (
    .RegDest(uc_w_1_regdest), .Branch(uc_w_1_branch), .MemtoReg(uc_w_1_memtoreg), .ALUOp(uc_w_1_aluop),
    .ALUSrc(uc_w_1_alusrc), .RegWrite(uc_w_1_regwrite), .PC_4(reg_if_id_1_out_5),
    .DATA_RS(banco_registradores_1_r1), .DATA_RT(banco_registradores_1_r2), .IMEXT(bit_extender_1_out),
    .RT(reg_if_id_1_out_6[25:21]), .RD(reg_if_id_1_out_6[15:11]), .RegDest_2(reg_id_ex_1_regdest_2),
    .Branch_2(reg_id_ex_1_branch_2), .MemtoReg_2(reg_id_ex_1_memtoreg_2), .ALUOp_2(reg_id_ex_1_aluop_2),
    .ALUSrc_2(reg_id_ex_1_alusrc_2), .RegWrite_2(reg_id_ex_1_regwrite_2), .PC_4_2(reg_id_ex_1_pc_4_2),
    .DATA_RS_2(reg_id_ex_1_data_rs_2), .DATA_RT_2(reg_id_ex_1_data_rt_2), .IMEXT_2(reg_id_ex_1_imext_2),
    .RT_2(reg_id_ex_1_rt_2), .RD_2(reg_id_ex_1_rd_2), .CLK(clock_1_out), .MemWrite(uc_w_1_memwrite),
    .MemWrite_2(reg_id_ex_1_memwrite_2), .RS(reg_if_id_1_out_6[25:21]), .RS_2(reg_id_ex_1_rs_2),
    .Jump(uc_w_1_jump), .Jump_2(reg_id_ex_1_jump_2), .BRANCH_SELECT(uc_w_1_branch_select),
    .BRANCH_SELECT_2(reg_id_ex_1_branch_select_2), .MEMREAD(uc_w_1_memread),
    .MEMREAD_2(reg_id_ex_1_memread_2), .STALL(unid_hazard_1_stall));
  and and_2 (and_2_out, xor_1_out, reg_id_ex_1_branch_2);
  xor xor_1 (xor_1_out, reg_id_ex_1_branch_select_2, ula_1_igual);
  Multiplexer #(.width(5), .enable("false")) multiplexer_3 (
    .in0(reg_id_ex_1_rt_2), .in1(reg_id_ex_1_rd_2), .out(multiplexer_3_out), .sel(reg_id_ex_1_regdest_2));
  Shifter #(.width(32)) shifter_1 (.in(reg_id_ex_1_imext_2), .\dist (5'b00010), .out(shifter_1_out));
  ALU_CONTROL alu_control_1 (.in_1(reg_id_ex_1_imext_2[5:0]), .out_3(alu_control_1_out_3), .in_2(reg_id_ex_1_aluop_2));
  Adder #(.width(32)) adder_3 (.a(reg_id_ex_1_pc_4_2), .b(shifter_1_out), .out(adder_3_out));  // open: cin, cout
  Multiplexer #(.select(2), .width(32), .enable("false")) multiplexer_4 (
    .in0(reg_id_ex_1_data_rs_2), .in1(multiplexer_7_out), .in2(reg_ex_mem_1_alu_out_2),
    .out(multiplexer_4_out), .sel(fowarding_1_forward_a));  // open: in3
  Multiplexer #(.select(2), .width(32), .enable("false")) multiplexer_5 (
    .in0(reg_id_ex_1_data_rt_2), .in1(multiplexer_7_out), .in2(reg_ex_mem_1_alu_out_2),
    .out(multiplexer_5_out), .sel(fowarding_1_forward_b));  // open: in3
  Multiplexer #(.width(32), .enable("false")) multiplexer_6 (
    .in0(multiplexer_5_out), .in1(reg_id_ex_1_imext_2), .out(multiplexer_6_out), .sel(reg_id_ex_1_alusrc_2));
  FOWARDING fowarding_1 (
    .REG_RS(reg_id_ex_1_rs_2), .REG_RT(reg_id_ex_1_rt_2), .FORWARD_A(fowarding_1_forward_a),
    .MEMWRITE(reg_ex_mem_1_memory_write_2), .REG_RD(reg_mem_wb_1_write_register_2),
    .FORWARD_B(fowarding_1_forward_b), .WRITE_WB_STAGE(reg_mem_wb_1_reg_write_2),
    .REG_RD_MEM(reg_ex_mem_1_write_register_2));
  ULA ula_1 (
    .Resultado(ula_1_resultado), .OP(alu_control_1_out_3), .B(multiplexer_6_out), .A(multiplexer_4_out),
    .igual(ula_1_igual));
  REG_EX_MEM reg_ex_mem_1 (
    .BRANCH(reg_id_ex_1_branch_2), .MEMTOREG(reg_id_ex_1_memtoreg_2), .MEMORY_WRITE(reg_id_ex_1_memwrite_2),
    .REGWRITE(reg_id_ex_1_regwrite_2), .BRANCH_ADDRESS(adder_3_out), .ALU_OUT(ula_1_resultado),
    .DATA_RT(multiplexer_5_out), .WRITE_REGISTER(multiplexer_3_out), .MEMTOREG_2(reg_ex_mem_1_memtoreg_2),
    .MEMORY_WRITE_2(reg_ex_mem_1_memory_write_2), .REGWRITE_2(reg_ex_mem_1_regwrite_2),
    .BRANCH_ADDRESS_2(reg_ex_mem_1_branch_address_2), .ALU_OUT_2(reg_ex_mem_1_alu_out_2),
    .DATA_RT_2(reg_ex_mem_1_data_rt_2), .WRITE_REGISTER_2(reg_ex_mem_1_write_register_2), .CLK(clock_1_out),
    .zero(ula_1_igual));  // open: BRANCH_2, zero_2
  RAM #(.addrWidth(16), .dataWidth(32), .bus("separate"), .Select("high"), .simpleMode("false")) DATA_MEMORY (
    .addr(reg_ex_mem_1_alu_out_2[17:2]), .din(reg_ex_mem_1_data_rt_2), .data(DATA_MEMORY_data),
    .str(reg_ex_mem_1_memory_write_2), .clk(clock_1_out));  // open: sel, ld, clr
  REG_MEM_WB reg_mem_wb_1 (
    .REG_WRITE(reg_ex_mem_1_regwrite_2), .MEMTOREG(reg_ex_mem_1_memtoreg_2), .MEM_OUT(DATA_MEMORY_data),
    .ALU_OUT(reg_ex_mem_1_alu_out_2), .WRITE_REGISTER(reg_ex_mem_1_write_register_2),
    .REG_WRITE_2(reg_mem_wb_1_reg_write_2), .MEMTOREG_2(reg_mem_wb_1_memtoreg_2),
    .MEM_OUT_2(reg_mem_wb_1_mem_out_2), .ALU_OUT_2(reg_mem_wb_1_alu_out_2),
    .WRITE_REGISTER_2(reg_mem_wb_1_write_register_2), .CLK(clock_1_out));
  Multiplexer #(.width(32), .enable("false")) multiplexer_7 (
    .in0(reg_mem_wb_1_alu_out_2), .in1(reg_mem_wb_1_mem_out_2), .out(multiplexer_7_out),
    .sel(reg_mem_wb_1_memtoreg_2));

  // Notes on the sheet:
  //   JR
  //   LINK
  //   MEMREAD
  //   BRANCH_SELECT
  //   RegDest
  //   JUMP
  //   RegWrite
  //   Branch
  //   MemtoReg
  //   ALUOp
  //   MemWrite
  //   ALUSrc
endmodule

module banco_registradores (
  input  [4:0] R1_num,
  input  [4:0] R2_num,
  input  [4:0] RW,
  input  [31:0] Din,
  input  WE,
  input  clk,
  input  [31:0] JAL,
  input  LINK,
  output [31:0] R1,
  output [31:0] R2
);

  wire demultiplexer_1_out0, demultiplexer_1_out1, demultiplexer_1_out2, demultiplexer_1_out3,
       demultiplexer_2_out0, demultiplexer_2_out1, demultiplexer_2_out2, demultiplexer_2_out3,
       demultiplexer_2_out4, demultiplexer_2_out5, demultiplexer_2_out6, demultiplexer_2_out7,
       demultiplexer_3_out0, demultiplexer_3_out1, demultiplexer_3_out2, demultiplexer_3_out3,
       demultiplexer_3_out4, demultiplexer_3_out5, demultiplexer_3_out6, demultiplexer_3_out7,
       demultiplexer_4_out0, demultiplexer_4_out1, demultiplexer_4_out2, demultiplexer_4_out3,
       demultiplexer_4_out4, demultiplexer_4_out5, demultiplexer_4_out6, demultiplexer_4_out7,
       demultiplexer_5_out0, demultiplexer_5_out1, demultiplexer_5_out2, demultiplexer_5_out3,
       demultiplexer_5_out4, demultiplexer_5_out5, demultiplexer_5_out6, demultiplexer_5_out7, or_1_out;
  wire [31:0] _0__Zero_q, _1__at_q, _3__v1_q, _5__a1_q, _6__a2_q, _7__a3_q, _8__t0_q, _9__t1_q, _10__t2_q,
       _11__t3_q, _12__t4_q, _13__t5_q, _14__t6_q, _15__t7_q, _19__s3_q, _20__s4_q, _21__s5_q, _22__s6_q,
       _23__s7_q, _24__t8_q, _25__t9_q, _26__k0_q, _27__k1_q, _28__gp_q, _29__sp_q, _30__fp_q, a0,
       multiplexer_1_out, ra, s0, s1, s2, v0;

  Demultiplexer #(.select(2), .disabled(0)) demultiplexer_1 (
    .out0(demultiplexer_1_out0), .out1(demultiplexer_1_out1), .out2(demultiplexer_1_out2),
    .out3(demultiplexer_1_out3), .in(1'b1), .sel(RW[4:3]), .en(WE));
  Demultiplexer #(.select(3), .disabled(0)) demultiplexer_2 (
    .out0(demultiplexer_2_out0), .out1(demultiplexer_2_out1), .out2(demultiplexer_2_out2),
    .out3(demultiplexer_2_out3), .out4(demultiplexer_2_out4), .out5(demultiplexer_2_out5),
    .out6(demultiplexer_2_out6), .out7(demultiplexer_2_out7), .in(1'b1), .sel(RW[2:0]),
    .en(demultiplexer_1_out0));
  Demultiplexer #(.select(3), .disabled(0)) demultiplexer_3 (
    .out0(demultiplexer_3_out0), .out1(demultiplexer_3_out1), .out2(demultiplexer_3_out2),
    .out3(demultiplexer_3_out3), .out4(demultiplexer_3_out4), .out5(demultiplexer_3_out5),
    .out6(demultiplexer_3_out6), .out7(demultiplexer_3_out7), .in(1'b1), .sel(RW[2:0]),
    .en(demultiplexer_1_out1));
  Demultiplexer #(.select(3), .disabled(0)) demultiplexer_4 (
    .out0(demultiplexer_4_out0), .out1(demultiplexer_4_out1), .out2(demultiplexer_4_out2),
    .out3(demultiplexer_4_out3), .out4(demultiplexer_4_out4), .out5(demultiplexer_4_out5),
    .out6(demultiplexer_4_out6), .out7(demultiplexer_4_out7), .in(1'b1), .sel(RW[2:0]),
    .en(demultiplexer_1_out2));
  Demultiplexer #(.select(3), .disabled(0)) demultiplexer_5 (
    .out0(demultiplexer_5_out0), .out1(demultiplexer_5_out1), .out2(demultiplexer_5_out2),
    .out3(demultiplexer_5_out3), .out4(demultiplexer_5_out4), .out5(demultiplexer_5_out5),
    .out6(demultiplexer_5_out6), .out7(demultiplexer_5_out7), .in(1'b1), .sel(RW[2:0]),
    .en(demultiplexer_1_out3));
  Register #(.width(32), .Select("low")) _0__Zero (
    .D(Din), .en(demultiplexer_2_out0), .Q(_0__Zero_q));  // open: clk, clr
  Register #(.width(32), .Select("low")) _8__t0 (
    .D(Din), .en(demultiplexer_3_out0), .Q(_8__t0_q), .clk(clk));  // open: clr
  Register #(.width(32), .Select("low")) _16__s0 (.D(Din), .en(demultiplexer_4_out0), .Q(s0), .clk(clk));  // open: clr
  Register #(.width(32), .Select("low")) _24__t8 (
    .D(Din), .en(demultiplexer_5_out0), .Q(_24__t8_q), .clk(clk));  // open: clr
  Register #(.width(32), .Select("low")) _1__at (
    .D(Din), .en(demultiplexer_2_out1), .Q(_1__at_q), .clk(clk));  // open: clr
  Register #(.width(32), .Select("low")) _9__t1 (
    .D(Din), .en(demultiplexer_3_out1), .Q(_9__t1_q), .clk(clk));  // open: clr
  Register #(.width(32), .Select("low")) _17__s1 (.D(Din), .en(demultiplexer_4_out1), .Q(s1), .clk(clk));  // open: clr
  Register #(.width(32), .Select("low")) _25__t9 (
    .D(Din), .en(demultiplexer_5_out1), .Q(_25__t9_q), .clk(clk));  // open: clr
  Register #(.width(32), .Select("low")) _2__v0 (.D(Din), .en(demultiplexer_2_out2), .Q(v0), .clk(clk));  // open: clr
  Register #(.width(32), .Select("low")) _10__t2 (
    .D(Din), .en(demultiplexer_3_out2), .Q(_10__t2_q), .clk(clk));  // open: clr
  Register #(.width(32), .Select("low")) _18__s2 (.D(Din), .en(demultiplexer_4_out2), .Q(s2), .clk(clk));  // open: clr
  Register #(.width(32), .Select("low")) _26__k0 (
    .D(Din), .en(demultiplexer_5_out2), .Q(_26__k0_q), .clk(clk));  // open: clr
  Register #(.width(32), .Select("low")) _3__v1 (
    .D(Din), .en(demultiplexer_2_out3), .Q(_3__v1_q), .clk(clk));  // open: clr
  Register #(.width(32), .Select("low")) _11__t3 (
    .D(Din), .en(demultiplexer_3_out3), .Q(_11__t3_q), .clk(clk));  // open: clr
  Register #(.width(32), .Select("low")) _19__s3 (
    .D(Din), .en(demultiplexer_4_out3), .Q(_19__s3_q), .clk(clk));  // open: clr
  Register #(.width(32), .Select("low")) _27__k1 (
    .D(Din), .en(demultiplexer_5_out3), .Q(_27__k1_q), .clk(clk));  // open: clr
  Register #(.width(32), .Select("low")) _4__a0 (.D(Din), .en(demultiplexer_2_out4), .Q(a0), .clk(clk));  // open: clr
  Register #(.width(32), .Select("low")) _12__t4 (
    .D(Din), .en(demultiplexer_3_out4), .Q(_12__t4_q), .clk(clk));  // open: clr
  Register #(.width(32), .Select("low")) _20__s4 (
    .D(Din), .en(demultiplexer_4_out4), .Q(_20__s4_q), .clk(clk));  // open: clr
  Register #(.width(32), .Select("low")) _28__gp (
    .D(Din), .en(demultiplexer_5_out4), .Q(_28__gp_q), .clk(clk));  // open: clr
  Register #(.width(32), .Select("low")) _5__a1 (
    .D(Din), .en(demultiplexer_2_out5), .Q(_5__a1_q), .clk(clk));  // open: clr
  Register #(.width(32), .Select("low")) _13__t5 (
    .D(Din), .en(demultiplexer_3_out5), .Q(_13__t5_q), .clk(clk));  // open: clr
  Register #(.width(32), .Select("low")) _21__s5 (
    .D(Din), .en(demultiplexer_4_out5), .Q(_21__s5_q), .clk(clk));  // open: clr
  Register #(.width(32), .Select("low")) _29__sp (
    .D(Din), .en(demultiplexer_5_out5), .Q(_29__sp_q), .clk(clk));  // open: clr
  Register #(.width(32), .Select("low")) _6__a2 (
    .D(Din), .en(demultiplexer_2_out6), .Q(_6__a2_q), .clk(clk));  // open: clr
  Register #(.width(32), .Select("low")) _14__t6 (
    .D(Din), .en(demultiplexer_3_out6), .Q(_14__t6_q), .clk(clk));  // open: clr
  Register #(.width(32), .Select("low")) _22__s6 (
    .D(Din), .en(demultiplexer_4_out6), .Q(_22__s6_q), .clk(clk));  // open: clr
  Register #(.width(32), .Select("low")) _30__fp (
    .D(Din), .en(demultiplexer_5_out6), .Q(_30__fp_q), .clk(clk));  // open: clr
  or or_1 (or_1_out, demultiplexer_5_out7, LINK);
  Multiplexer #(.width(32), .enable("false")) multiplexer_1 (.in0(Din), .in1(JAL), .out(multiplexer_1_out), .sel(LINK));
  Register #(.width(32), .Select("low")) _7__a3 (
    .D(Din), .en(demultiplexer_2_out7), .Q(_7__a3_q), .clk(clk));  // open: clr
  Register #(.width(32), .Select("low")) _15__t7 (
    .D(Din), .en(demultiplexer_3_out7), .Q(_15__t7_q), .clk(clk));  // open: clr
  Register #(.width(32), .Select("low")) _23__s7 (
    .D(Din), .en(demultiplexer_4_out7), .Q(_23__s7_q), .clk(clk));  // open: clr
  Register #(.width(32), .Select("low")) _31__ra (
    .D(multiplexer_1_out), .en(or_1_out), .Q(ra), .clk(clk));  // open: clr
  Multiplexer #(.select(5), .width(32), .enable("false")) multiplexer_2 (
    .in0(_0__Zero_q), .in1(_1__at_q), .in2(v0), .in3(_3__v1_q), .in4(a0), .in5(_5__a1_q), .in6(_6__a2_q),
    .in7(_7__a3_q), .in8(_8__t0_q), .in9(_9__t1_q), .in10(_10__t2_q), .in11(_11__t3_q), .in12(_12__t4_q),
    .in13(_13__t5_q), .in14(_14__t6_q), .in15(_15__t7_q), .in16(s0), .in17(s1), .in18(s2), .in19(_19__s3_q),
    .in20(_20__s4_q), .in21(_21__s5_q), .in22(_22__s6_q), .in23(_23__s7_q), .in24(_24__t8_q),
    .in25(_25__t9_q), .in26(_26__k0_q), .in27(_27__k1_q), .in28(_28__gp_q), .in29(_29__sp_q),
    .in30(_30__fp_q), .in31(ra), .out(R1), .sel(R1_num));
  Multiplexer #(.select(5), .width(32), .enable("false")) multiplexer_3 (
    .in0(_0__Zero_q), .in1(_1__at_q), .in2(v0), .in3(_3__v1_q), .in4(a0), .in5(_5__a1_q), .in6(_6__a2_q),
    .in7(_7__a3_q), .in8(_8__t0_q), .in9(_9__t1_q), .in10(_10__t2_q), .in11(_11__t3_q), .in12(_12__t4_q),
    .in13(_13__t5_q), .in14(_14__t6_q), .in15(_15__t7_q), .in16(s0), .in17(s1), .in18(s2), .in19(_19__s3_q),
    .in20(_20__s4_q), .in21(_21__s5_q), .in22(_22__s6_q), .in23(_23__s7_q), .in24(_24__t8_q),
    .in25(_25__t9_q), .in26(_26__k0_q), .in27(_27__k1_q), .in28(_28__gp_q), .in29(_29__sp_q),
    .in30(_30__fp_q), .in31(ra), .out(R2), .sel(R2_num));

  // Other names for the same wires on the sheet: reg1[31:0] = R1; reg1_num[4:0] = R1_num; reg2[31:0] = R2;
  //   reg2_num[4:0] = R2_num; write_data[31:0] = Din; write_reg_num[4:0] = RW

  // Notes on the sheet:
  //   Input
  //   Output
endmodule

module ULA (
  input  [31:0] A,
  input  [31:0] B,
  input  [5:0] OP,
  output igual,
  output [31:0] Resultado
);

  wire comparator_1_lt;
  wire [31:0] adder_1_out, and_1_out, bit_extender_1_out, divider_1_out, multiplier_1_out, or_1_out,
       shifter_1_out, shifter_2_out, subtractor_1_out;

  Adder #(.width(32)) adder_1 (.a(A), .b(B), .out(adder_1_out));  // open: cin, cout
  Subtractor #(.width(32)) subtractor_1 (.a(A), .b(B), .out(subtractor_1_out));  // open: bin, bout
  Multiplier #(.width(32)) multiplier_1 (.a(A), .b(B), .out(multiplier_1_out));  // open: cin, cout
  Divider #(.width(32)) divider_1 (.a(A), .b(B), .out(divider_1_out));  // open: upper, rem
  Comparator #(.width(32)) comparator_1 (.a(A), .b(B), .eq(igual), .lt(comparator_1_lt));  // open: gt
  assign and_1_out = A & B;  // AND_Gate and_1, 32 bits wide
  assign or_1_out = A | B;  // OR_Gate or_1, 32 bits wide
  Shifter #(.width(32)) shifter_1 (.in(A), .\dist (B[9:5]), .out(shifter_1_out));
  Shifter #(.width(32), .shift("lr")) shifter_2 (.in(A), .\dist (B[9:5]), .out(shifter_2_out));
  assign bit_extender_1_out = {{31{1'b0}}, comparator_1_lt};  // Bit_Extender bit_extender_1
  Multiplexer #(.select(4), .width(32), .enable("false")) multiplexer_1 (
    .in0(adder_1_out), .in1(subtractor_1_out), .in2(multiplier_1_out), .in3(divider_1_out), .in4(and_1_out),
    .in5(or_1_out), .in6(shifter_1_out), .in7(shifter_2_out), .in8(bit_extender_1_out), .out(Resultado),
    .sel(OP[3:0]));  // open: in9, in10, in11, in12, in13, in14, in15

  // Notes on the sheet:
  //   SHAMT
endmodule

module UC (
  input  UC5,
  input  UC4,
  input  UC3,
  input  UC2,
  input  UC1,
  input  UC0,
  output REGDEST,
  output JUMP,
  output MEMREAD,
  output BRANCH,
  output MEMTOREG,
  output ULA0P0,
  output ULA0P1,
  output ULAOPSRC,
  output MEM_WR,
  output ULASRC,
  output WR,
  output BRANCH_SELECT,
  output JR,
  output Link
);

  wire and_2_out, and_3_out, and_4_out, and_5_out, and_6_out, and_7_out, and_8_out, and_9_out, and_11_out,
       and_12_out, and_13_out, and_14_out, and_15_out, and_16_out, and_17_out, and_18_out, and_19_out,
       and_20_out, and_21_out, and_22_out, and_23_out, and_24_out, and_25_out, and_26_out, and_27_out,
       and_28_out, and_29_out, and_30_out, and_31_out, and_32_out, and_33_out, and_34_out, and_35_out,
       and_36_out, and_37_out, and_38_out, and_39_out, and_40_out, and_41_out, and_42_out, and_43_out,
       and_44_out, and_45_out, and_46_out, and_47_out, and_48_out, and_49_out, and_50_out, and_51_out,
       and_52_out, not_1_out, not_2_out, not_3_out, not_4_out, not_5_out, not_6_out, not_7_out, not_8_out,
       not_9_out, not_10_out, not_11_out, not_12_out, not_13_out, not_14_out, not_15_out, not_16_out,
       not_17_out, not_18_out, not_19_out, not_20_out, not_21_out, not_22_out, not_23_out, not_24_out,
       not_25_out, not_26_out, not_27_out, not_28_out, not_29_out, not_30_out, not_31_out, not_32_out,
       not_33_out, not_34_out, not_35_out, not_36_out, not_37_out, not_38_out, not_39_out, not_40_out,
       not_41_out, not_42_out, not_43_out, not_44_out, not_45_out, not_46_out, not_47_out, not_48_out,
       not_49_out, not_50_out, not_51_out, not_52_out, not_53_out, not_54_out, not_55_out, not_56_out,
       not_57_out, not_58_out, not_59_out, not_60_out, not_61_out, not_62_out, not_63_out, not_64_out,
       not_65_out, not_66_out, not_67_out, not_68_out, not_69_out, not_70_out, not_71_out, not_72_out,
       not_73_out, not_74_out, not_75_out, not_76_out, not_77_out, not_78_out, not_79_out, not_80_out,
       not_81_out, not_82_out, not_83_out;

  and and_1 (MEMREAD, UC5, not_1_out, not_2_out, not_3_out, UC1, UC0);
  not not_1 (not_1_out, UC4);
  not not_2 (not_2_out, UC3);
  not not_3 (not_3_out, UC2);
  not not_4 (not_4_out, UC3);
  not not_5 (not_5_out, UC2);
  not not_6 (not_6_out, UC1);
  not not_7 (not_7_out, UC0);
  not not_8 (not_8_out, UC1);
  not not_9 (not_9_out, UC0);
  not not_10 (not_10_out, UC5);
  not not_11 (not_11_out, UC4);
  not not_12 (not_12_out, UC3);
  not not_13 (not_13_out, UC0);
  not not_14 (not_14_out, UC5);
  not not_15 (not_15_out, UC4);
  not not_16 (not_16_out, UC3);
  not not_17 (not_17_out, UC1);
  not not_18 (not_18_out, UC5);
  not not_19 (not_19_out, UC4);
  not not_20 (not_20_out, UC2);
  not not_21 (not_21_out, UC1);
  not not_22 (not_22_out, UC5);
  not not_23 (not_23_out, UC4);
  not not_24 (not_24_out, UC2);
  not not_25 (not_25_out, UC0);
  not not_26 (not_26_out, UC5);
  not not_27 (not_27_out, UC4);
  not not_28 (not_28_out, UC2);
  not not_29 (not_29_out, UC1);
  not not_30 (not_30_out, UC0);
  not not_31 (not_31_out, UC3);
  not not_32 (not_32_out, UC0);
  not not_33 (not_33_out, UC3);
  not not_34 (not_34_out, UC1);
  not not_35 (not_35_out, UC1);
  not not_36 (not_36_out, UC0);
  not not_37 (not_37_out, UC0);
  not not_38 (not_38_out, UC1);
  not not_39 (not_39_out, UC0);
  not not_40 (not_40_out, UC1);
  not not_41 (not_41_out, UC3);
  not not_42 (not_42_out, UC2);
  not not_43 (not_43_out, UC3);
  not not_44 (not_44_out, UC1);
  not not_45 (not_45_out, UC1);
  not not_46 (not_46_out, UC2);
  not not_47 (not_47_out, UC1);
  not not_48 (not_48_out, UC2);
  not not_49 (not_49_out, UC1);
  not not_50 (not_50_out, UC1);
  not not_51 (not_51_out, UC3);
  not not_52 (not_52_out, UC0);
  not not_53 (not_53_out, UC3);
  not not_54 (not_54_out, UC2);
  not not_55 (not_55_out, UC1);
  and and_2 (and_2_out, UC3, UC2, UC0);
  and and_3 (and_3_out, UC3, UC2, UC1);
  and and_4 (and_4_out, UC4, UC3);
  and and_5 (and_5_out, UC5, UC3);
  not not_56 (not_56_out, UC3);
  not not_57 (not_57_out, UC2);
  not not_58 (not_58_out, UC3);
  not not_59 (not_59_out, UC3);
  not not_60 (not_60_out, UC0);
  not not_61 (not_61_out, UC5);
  not not_62 (not_62_out, UC4);
  not not_63 (not_63_out, UC3);
  not not_64 (not_64_out, UC2);
  not not_65 (not_65_out, UC5);
  not not_66 (not_66_out, UC4);
  not not_67 (not_67_out, UC3);
  not not_68 (not_68_out, UC1);
  not not_69 (not_69_out, UC0);
  not not_70 (not_70_out, UC5);
  not not_71 (not_71_out, UC4);
  not not_72 (not_72_out, UC3);
  not not_73 (not_73_out, UC5);
  not not_74 (not_74_out, UC4);
  not not_75 (not_75_out, UC2);
  not not_76 (not_76_out, UC0);
  not not_77 (not_77_out, UC5);
  not not_78 (not_78_out, UC4);
  not not_79 (not_79_out, UC2);
  not not_80 (not_80_out, UC5);
  not not_81 (not_81_out, UC4);
  not not_82 (not_82_out, UC1);
  not not_83 (not_83_out, UC0);
  and and_6 (and_6_out, not_4_out, not_5_out, not_6_out, not_7_out);
  and and_7 (and_7_out, UC2, not_8_out, UC0);
  and and_8 (and_8_out, UC2, UC1, not_9_out);
  and and_9 (and_9_out, UC3, UC2, UC1);
  and and_10 (JUMP, not_10_out, not_11_out, not_12_out, UC2, UC1, not_13_out);
  and and_11 (and_11_out, not_14_out, not_15_out, not_16_out, UC2, not_17_out, UC0);
  and and_12 (and_12_out, not_18_out, not_19_out, UC3, not_20_out, not_21_out, UC0);
  and and_13 (and_13_out, not_22_out, not_23_out, UC3, not_24_out, UC1, not_25_out);
  and and_14 (and_14_out, UC2, UC1);
  and and_15 (and_15_out, not_26_out, not_27_out, UC3, not_28_out, not_29_out, not_30_out);
  and and_16 (and_16_out, not_31_out, UC1, not_32_out);
  and and_17 (and_17_out, not_33_out, UC2, not_34_out);
  and and_18 (and_18_out, UC2, not_35_out, UC0);
  and and_19 (and_19_out, UC2, UC1, not_36_out);
  and and_20 (and_20_out, UC4, UC1, not_37_out);
  and and_21 (and_21_out, UC4, UC2, not_38_out);
  and and_22 (and_22_out, UC5, UC1, not_39_out);
  and and_23 (and_23_out, UC5, UC2, not_40_out);
  and and_24 (and_24_out, not_41_out, not_42_out, UC1, UC0);
  and and_25 (and_25_out, not_43_out, UC2, not_44_out);
  and and_26 (and_26_out, UC2, not_45_out, UC0);
  and and_27 (and_27_out, UC4, not_46_out, UC1, UC0);
  and and_28 (and_28_out, UC4, UC2, not_47_out);
  and and_29 (and_29_out, UC5, not_48_out, UC1, UC0);
  and and_30 (and_30_out, UC5, UC2, not_49_out);
  and and_31 (and_31_out, not_50_out, UC0);
  and and_32 (and_32_out, not_51_out, UC1);
  and and_33 (and_33_out, UC1, not_52_out);
  and and_34 (and_34_out, not_53_out, UC2);
  and and_35 (and_35_out, UC2, UC1);
  and and_36 (and_36_out, UC3, not_54_out, not_55_out);
  and and_37 (and_37_out, UC4, UC3);
  and and_38 (and_38_out, UC5, UC3);
  or or_1 (MEM_WR, and_2_out, and_3_out, and_4_out, and_5_out);
  and and_39 (and_39_out, not_56_out, not_57_out, UC0);
  and and_40 (and_40_out, not_58_out, UC1);
  and and_41 (and_41_out, not_59_out, UC2, not_60_out);
  and and_42 (and_42_out, UC2, UC1);
  and and_43 (and_43_out, UC3, UC2, UC0);
  and and_44 (and_44_out, UC4, UC0);
  and and_45 (and_45_out, UC4, UC1);
  and and_46 (and_46_out, UC4, UC2);
  and and_47 (and_47_out, UC5, UC0);
  and and_48 (and_48_out, UC5, UC1);
  and and_49 (and_49_out, UC5, UC2);
  and and_50 (and_50_out, not_61_out, not_62_out, not_63_out, not_64_out);
  and and_51 (and_51_out, not_65_out, not_66_out, not_67_out, not_68_out, not_69_out);
  and and_52 (and_52_out, not_70_out, not_71_out, not_72_out, UC1, UC0);
  and and_53 (BRANCH_SELECT, not_73_out, not_74_out, UC3, not_75_out, UC1, not_76_out);
  and and_54 (JR, not_77_out, not_78_out, UC3, not_79_out, UC1, UC0);
  and and_55 (Link, not_80_out, not_81_out, UC3, UC2, not_82_out, not_83_out);
  or or_2 (REGDEST, and_6_out, and_7_out, and_8_out, and_9_out, UC4, UC5);
  or or_3 (BRANCH, and_11_out, and_12_out, and_13_out);
  or or_4 (MEMTOREG, and_14_out, and_15_out);
  or or_5 (ULA0P0, and_16_out, and_17_out, and_18_out, and_19_out, and_20_out, and_21_out, and_22_out, and_23_out);
  or or_6 (ULA0P1, and_24_out, and_25_out, and_26_out, and_27_out, and_28_out, and_29_out, and_30_out);
  or or_7 (ULAOPSRC, and_31_out, and_32_out, and_33_out, and_34_out, and_35_out, and_36_out, and_37_out, and_38_out);
  or or_8 (ULASRC, and_39_out, and_40_out, and_41_out, and_42_out, and_43_out, and_44_out, and_45_out, and_46_out, and_47_out, and_48_out, and_49_out);
  or or_9 (WR, and_50_out, and_51_out, and_52_out);
endmodule

// ULAOP
module OPULA (
  input  OPCOD0,
  input  OPCOD1,
  input  OPCOD2,
  input  OPCOD3,
  input  OPCOD4,
  input  OPCOD5,
  input  FUNC0,
  input  FUNC1,
  input  FUNC2,
  input  FUNC3,
  input  FUNC4,
  input  FUNC5,
  output ULAOP0,
  output ULAOP1,
  output ULAOP2,
  output ULAOP3
);
endmodule

// UC
module UC_W (
  input  [5:0] in_1,
  output REGDEST,
  output JUMP,
  output BRANCH,
  output MEMTOREG,
  output [2:0] ALUOP,
  output MEMWRITE,
  output ALUSRC,
  output REGWRITE,
  output BRANCH_SELECT,
  output JR,
  output LINK,
  output MEMREAD
);

  UC uc_1 (
    .UC5(in_1[5]), .UC4(in_1[4]), .UC3(in_1[3]), .UC2(in_1[2]), .UC1(in_1[1]), .REGDEST(REGDEST),
    .UC0(in_1[0]), .JUMP(JUMP), .BRANCH(BRANCH), .MEMTOREG(MEMTOREG), .ULA0P0(ALUOP[0]), .ULA0P1(ALUOP[1]),
    .ULAOPSRC(ALUOP[2]), .MEM_WR(MEMWRITE), .ULASRC(ALUSRC), .WR(REGWRITE), .BRANCH_SELECT(BRANCH_SELECT),
    .JR(JR), .Link(LINK), .MEMREAD(MEMREAD));
endmodule

// ALUCONTROL
module ALU_CONTROL (
  input  [5:0] in_1,
  input  [2:0] in_2,
  output [5:0] out_3
);

  wire [5:0] bit_extender_1_out;

  assign bit_extender_1_out = {{4{1'b0}}, in_2[1:0]};  // Bit_Extender bit_extender_1
  Multiplexer #(.width(6), .enable("false")) multiplexer_1 (
    .in0(in_1), .in1(bit_extender_1_out), .out(out_3), .sel(in_2[2]));
endmodule

// IF/ID
module REG_IF_ID (
  input  [31:0] in_1,
  input  [31:0] in_2,
  input  STALL,
  input  CLK,
  output [31:0] out_5,
  output [31:0] out_6
);

  Register #(.width(32), .Select("low")) register_1 (.D(in_1), .en(STALL), .Q(out_5), .clk(CLK));  // open: clr
  Register #(.width(32), .Select("low")) register_2 (.D(in_2), .en(STALL), .Q(out_6), .clk(CLK));  // open: clr
endmodule

// ID/EX
module REG_ID_EX (
  input  RegDest,
  input  Branch,
  input  MemtoReg,
  input  [2:0] ALUOp,
  input  MemWrite,
  input  ALUSrc,
  input  RegWrite,
  input  MEMREAD,
  input  [31:0] PC_4,
  input  [31:0] DATA_RS,
  input  [31:0] DATA_RT,
  input  [31:0] IMEXT,
  input  [4:0] RS,
  input  [4:0] RT,
  input  [4:0] RD,
  input  Jump,
  input  BRANCH_SELECT,
  input  STALL,
  input  CLK,
  output RegDest_2,
  output Branch_2,
  output MemtoReg_2,
  output [2:0] ALUOp_2,
  output MemWrite_2,
  output ALUSrc_2,
  output RegWrite_2,
  output MEMREAD_2,
  output [31:0] PC_4_2,
  output [31:0] DATA_RS_2,
  output [31:0] DATA_RT_2,
  output [31:0] IMEXT_2,
  output [4:0] RS_2,
  output [4:0] RT_2,
  output [4:0] RD_2,
  output Jump_2,
  output BRANCH_SELECT_2
);

  wire multiplexer_2_out, multiplexer_3_out, multiplexer_4_out, multiplexer_5_out, multiplexer_9_out,
       multiplexer_10_out, multiplexer_11_out, multiplexer_12_out, multiplexer_13_out;
  wire [2:0] multiplexer_1_out;
  wire [4:0] multiplexer_6_out, multiplexer_7_out, multiplexer_8_out;
  wire [31:0] multiplexer_14_out, multiplexer_15_out, multiplexer_16_out, multiplexer_17_out;

  Multiplexer #(.width(3), .enable("false")) multiplexer_1 (
    .in0(ALUOp), .in1(3'b000), .out(multiplexer_1_out), .sel(STALL));
  Multiplexer #(.enable("false")) multiplexer_2 (.in0(MemWrite), .in1(1'b0), .out(multiplexer_2_out), .sel(STALL));
  Multiplexer #(.enable("false")) multiplexer_3 (.in0(ALUSrc), .in1(1'b0), .out(multiplexer_3_out), .sel(STALL));
  Multiplexer #(.enable("false")) multiplexer_4 (.in0(RegWrite), .in1(1'b0), .out(multiplexer_4_out), .sel(STALL));
  Multiplexer #(.enable("false")) multiplexer_5 (.in0(MEMREAD), .in1(1'b0), .out(multiplexer_5_out), .sel(STALL));
  Multiplexer #(.width(5), .enable("false")) multiplexer_6 (
    .in0(RS), .in1({5{1'b0}}), .out(multiplexer_6_out), .sel(STALL));
  Multiplexer #(.width(5), .enable("false")) multiplexer_7 (
    .in0(RT), .in1({5{1'b0}}), .out(multiplexer_7_out), .sel(STALL));
  Multiplexer #(.width(5), .enable("false")) multiplexer_8 (
    .in0(RD), .in1({5{1'b0}}), .out(multiplexer_8_out), .sel(STALL));
  Multiplexer #(.enable("false")) multiplexer_9 (.in0(Jump), .in1(1'b0), .out(multiplexer_9_out), .sel(STALL));
  Multiplexer #(.enable("false")) multiplexer_10 (
    .in0(BRANCH_SELECT), .in1(1'b0), .out(multiplexer_10_out), .sel(STALL));
  Multiplexer #(.enable("false")) multiplexer_11 (.in0(RegDest), .in1(1'b0), .out(multiplexer_11_out), .sel(STALL));
  Multiplexer #(.enable("false")) multiplexer_12 (.in0(Branch), .in1(1'b0), .out(multiplexer_12_out), .sel(STALL));
  Multiplexer #(.enable("false")) multiplexer_13 (.in0(MemtoReg), .in1(1'b0), .out(multiplexer_13_out), .sel(STALL));
  Multiplexer #(.width(32), .enable("false")) multiplexer_14 (
    .in0(PC_4), .in1({32{1'b0}}), .out(multiplexer_14_out), .sel(STALL));
  Multiplexer #(.width(32), .enable("false")) multiplexer_15 (
    .in0(DATA_RS), .in1({32{1'b0}}), .out(multiplexer_15_out), .sel(STALL));
  Multiplexer #(.width(32), .enable("false")) multiplexer_16 (
    .in0(DATA_RT), .in1({32{1'b0}}), .out(multiplexer_16_out), .sel(STALL));
  Multiplexer #(.width(32), .enable("false")) multiplexer_17 (
    .in0(IMEXT), .in1({32{1'b0}}), .out(multiplexer_17_out), .sel(STALL));
  Register #(.width(1), .Select("low")) register_1 (.D(multiplexer_11_out), .Q(RegDest_2), .clk(CLK));  // open: en, clr
  Register #(.width(1), .Select("low")) register_2 (.D(multiplexer_12_out), .Q(Branch_2), .clk(CLK));  // open: en, clr
  Register #(.width(1), .Select("low")) register_3 (
    .D(multiplexer_13_out), .Q(MemtoReg_2), .clk(CLK));  // open: en, clr
  Register #(.width(3), .Select("low")) register_4 (.D(multiplexer_1_out), .Q(ALUOp_2), .clk(CLK));  // open: en, clr
  Register #(.width(1), .Select("low")) register_5 (.D(multiplexer_2_out), .Q(MemWrite_2), .clk(CLK));  // open: en, clr
  Register #(.width(1), .Select("low")) register_6 (.D(multiplexer_3_out), .Q(ALUSrc_2), .clk(CLK));  // open: en, clr
  Register #(.width(1), .Select("low")) register_7 (.D(multiplexer_4_out), .Q(RegWrite_2), .clk(CLK));  // open: en, clr
  Register #(.width(1), .Select("low")) register_8 (.D(multiplexer_5_out), .Q(MEMREAD_2), .clk(CLK));  // open: en, clr
  Register #(.width(32), .Select("low")) register_9 (.D(multiplexer_14_out), .Q(PC_4_2), .clk(CLK));  // open: en, clr
  Register #(.width(32), .Select("low")) register_10 (
    .D(multiplexer_15_out), .Q(DATA_RS_2), .clk(CLK));  // open: en, clr
  Register #(.width(32), .Select("low")) register_11 (
    .D(multiplexer_16_out), .Q(DATA_RT_2), .clk(CLK));  // open: en, clr
  Register #(.width(32), .Select("low")) register_12 (.D(multiplexer_17_out), .Q(IMEXT_2), .clk(CLK));  // open: en, clr
  Register #(.width(5), .Select("low")) register_13 (.D(multiplexer_6_out), .Q(RS_2), .clk(CLK));  // open: en, clr
  Register #(.width(5), .Select("low")) register_14 (.D(multiplexer_7_out), .Q(RT_2), .clk(CLK));  // open: en, clr
  Register #(.width(5), .Select("low")) register_15 (.D(multiplexer_8_out), .Q(RD_2), .clk(CLK));  // open: en, clr
  Register #(.width(1), .Select("low")) register_16 (.D(multiplexer_9_out), .Q(Jump_2), .clk(CLK));  // open: en, clr
  Register #(.width(1), .Select("low")) register_17 (
    .D(multiplexer_10_out), .Q(BRANCH_SELECT_2), .clk(CLK));  // open: en, clr
endmodule

// EX/MEM
module REG_EX_MEM (
  input  BRANCH,
  input  MEMTOREG,
  input  MEMORY_WRITE,
  input  REGWRITE,
  input  [31:0] BRANCH_ADDRESS,
  input  zero,
  input  [31:0] ALU_OUT,
  input  [31:0] DATA_RT,
  input  [4:0] WRITE_REGISTER,
  input  CLK,
  output BRANCH_2,
  output MEMTOREG_2,
  output MEMORY_WRITE_2,
  output REGWRITE_2,
  output [31:0] BRANCH_ADDRESS_2,
  output zero_2,
  output [31:0] ALU_OUT_2,
  output [31:0] DATA_RT_2,
  output [4:0] WRITE_REGISTER_2
);

  Register #(.width(1), .Select("low")) register_1 (.D(BRANCH), .Q(BRANCH_2), .clk(CLK));  // open: en, clr
  Register #(.width(1), .Select("low")) register_2 (.D(MEMTOREG), .Q(MEMTOREG_2), .clk(CLK));  // open: en, clr
  Register #(.width(1), .Select("low")) register_3 (.D(MEMORY_WRITE), .Q(MEMORY_WRITE_2), .clk(CLK));  // open: en, clr
  Register #(.width(1), .Select("low")) register_4 (.D(REGWRITE), .Q(REGWRITE_2), .clk(CLK));  // open: en, clr
  Register #(.width(32), .Select("low")) register_5 (
    .D(BRANCH_ADDRESS), .Q(BRANCH_ADDRESS_2), .clk(CLK));  // open: en, clr
  Register #(.width(1), .Select("low")) register_6 (.D(zero), .Q(zero_2), .clk(CLK));  // open: en, clr
  Register #(.width(32), .Select("low")) register_7 (.D(ALU_OUT), .Q(ALU_OUT_2), .clk(CLK));  // open: en, clr
  Register #(.width(32), .Select("low")) register_8 (.D(DATA_RT), .Q(DATA_RT_2), .clk(CLK));  // open: en, clr
  Register #(.width(5), .Select("low")) register_9 (
    .D(WRITE_REGISTER), .Q(WRITE_REGISTER_2), .clk(CLK));  // open: en, clr
endmodule

// MEM/WB
module REG_MEM_WB (
  input  REG_WRITE,
  input  MEMTOREG,
  input  [31:0] MEM_OUT,
  input  [31:0] ALU_OUT,
  input  [4:0] WRITE_REGISTER,
  input  CLK,
  output REG_WRITE_2,
  output MEMTOREG_2,
  output [31:0] MEM_OUT_2,
  output [31:0] ALU_OUT_2,
  output [4:0] WRITE_REGISTER_2
);

  Register #(.width(1), .Select("low")) register_1 (.D(REG_WRITE), .Q(REG_WRITE_2), .clk(CLK));  // open: en, clr
  Register #(.width(1), .Select("low")) register_2 (.D(MEMTOREG), .Q(MEMTOREG_2), .clk(CLK));  // open: en, clr
  Register #(.width(32), .Select("low")) register_3 (.D(MEM_OUT), .Q(MEM_OUT_2), .clk(CLK));  // open: en, clr
  Register #(.width(32), .Select("low")) register_4 (.D(ALU_OUT), .Q(ALU_OUT_2), .clk(CLK));  // open: en, clr
  Register #(.width(5), .Select("low")) register_5 (
    .D(WRITE_REGISTER), .Q(WRITE_REGISTER_2), .clk(CLK));  // open: en, clr
endmodule

// FWRD
module FOWARDING (
  input  WRITE_WB_STAGE,
  input  MEMWRITE,
  input  [4:0] REG_RD,
  input  [4:0] REG_RS,
  input  [4:0] REG_RT,
  input  [4:0] REG_RD_MEM,
  output [1:0] FORWARD_A,
  output [1:0] FORWARD_B
);

  wire comparator_1_eq, comparator_2_eq, comparator_3_eq, comparator_4_eq;
  wire [0:0] and_1_out, and_2_out;
  wire [1:1] and_3_out, and_4_out;

  Multiplexer #(.width(2), .enable("false")) multiplexer_1 (
    .in0({and_3_out[1], 1'b0}), .in1({1'b0, and_1_out[0]}), .out(FORWARD_A), .sel(MEMWRITE));
  Multiplexer #(.width(2), .enable("false")) multiplexer_2 (
    .in0({1'b0, and_2_out[0]}), .in1({and_4_out[1], 1'b0}), .out(FORWARD_B), .sel(MEMWRITE));
  Comparator #(.width(5)) comparator_1 (.a(REG_RD), .b(REG_RS), .eq(comparator_1_eq));  // open: gt, lt
  Comparator #(.width(5)) comparator_2 (.a(REG_RD), .b(REG_RT), .eq(comparator_2_eq));  // open: gt, lt
  Comparator #(.width(5)) comparator_3 (.a(REG_RD_MEM), .b(REG_RS), .eq(comparator_3_eq));  // open: gt, lt
  Comparator #(.width(5)) comparator_4 (.a(REG_RD_MEM), .b(REG_RT), .eq(comparator_4_eq));  // open: gt, lt
  and and_1 (and_1_out[0], WRITE_WB_STAGE, comparator_1_eq);
  and and_2 (and_2_out[0], WRITE_WB_STAGE, comparator_2_eq);
  and and_3 (and_3_out[1], MEMWRITE, comparator_3_eq);
  and and_4 (and_4_out[1], MEMWRITE, comparator_4_eq);
endmodule

// Hazard
module UNID_HAZARD (
  input  MEMREAD,
  input  [4:0] REG_RS_IF_ID,
  input  [4:0] REG_RT_IF_ID,
  input  [4:0] REG_RT_ID_EX,
  output STALL
);

  wire and_1_out, and_2_out, comparator_1_eq, comparator_2_eq;

  Comparator #(.width(5)) comparator_1 (.a(REG_RS_IF_ID), .b(REG_RT_ID_EX), .eq(comparator_1_eq));  // open: gt, lt
  Comparator #(.width(5)) comparator_2 (.a(REG_RT_ID_EX), .b(REG_RT_IF_ID), .eq(comparator_2_eq));  // open: gt, lt
  and and_1 (and_1_out, comparator_1_eq, MEMREAD);
  or or_1 (STALL, and_1_out, and_2_out);
  and and_2 (and_2_out, comparator_2_eq, MEMREAD);
endmodule
